// Logisim project 4bitadder.circ as structural Verilog: 1 circuit, main circuit main
module main (
  input  B3,
  input  B2,
  input  B1,
  input  B0,
  input  A3,
  input  A2,
  input  A1,
  input  A0,
  input  Cin,
  output Cout,
  output S3,
  output S2,
  output S1,
  output S0
);

  wire full_adder_2_cout, full_adder_3_cout, full_adder_4_cout;

  Full_Adder full_adder_1 (.Cout(Cout), .B(B3), .A(A3), .S(S3), .Cin(full_adder_2_cout));
  Full_Adder full_adder_2 (.Cout(full_adder_2_cout), .B(B2), .A(A2), .S(S2), .Cin(full_adder_3_cout));
  Full_Adder full_adder_3 (.Cout(full_adder_3_cout), .B(B1), .A(A1), .S(S1), .Cin(full_adder_4_cout));
  Full_Adder full_adder_4 (.Cout(full_adder_4_cout), .B(B0), .A(A0), .S(S0), .Cin(Cin));
endmodule
