// Logisim project BCD adder.circ as structural Verilog: 1 circuit, main circuit main
module main (
  input  A0,
  input  A1,
  input  A2,
  input  A3,
  input  B0,
  input  B1,
  input  B0_2,
  input  B3,
  input  Cin,
  output Cout,
  output S0,
  output S1,
  output S2,
  output S3
);

  wire and_1_out, and_2_out, main_1_cout, main_1_s0, main_1_s1, main_1_s2, main_1_s3;

  or or_1 (Cout, and_1_out, main_1_cout, and_2_out);
  and and_1 (and_1_out, main_1_s3, main_1_s2);
  and and_2 (and_2_out, main_1_s3, main_1_s1);
  _4bitadder_main main_1 (
    .B3(B3), .B2(B0_2), .B1(B1), .B0(B0), .A3(A3), .A2(A2), .A1(A1), .A0(A0), .Cout(main_1_cout), .Cin(Cin),
    .S3(main_1_s3), .S2(main_1_s2), .S1(main_1_s1), .S0(main_1_s0));
  _4bitadder_main main_2 (
    .B3(1'b0), .B2(Cout), .B1(Cout), .B0(1'b0), .A3(main_1_s3), .A2(main_1_s2), .A1(main_1_s1),
    .A0(main_1_s0), .Cin(1'b0), .S3(S3), .S2(S2), .S1(S1), .S0(S0));  // open: Cout
endmodule
