// Logisim project addersubtractor.circ as structural Verilog: 1 circuit, main circuit main
module main (
  input  B3,
  input  A3,
  input  B2,
  input  A2,
  input  B1,
  input  A1,
  input  B0,
  input  A0,
  input  Cin,
  output Cout,
  output S2,
  output S0,
  output S3,
  output S1
);

  wire full_adder_2_cout, full_adder_3_cout, full_adder_4_cout, xor_1_out, xor_2_out, xor_3_out, xor_4_out;

  xor xor_1 (xor_1_out, B3, Cin);
  Full_Adder full_adder_1 (.Cout(Cout), .B(xor_1_out), .A(A3), .S(S3), .Cin(full_adder_2_cout));
  xor xor_2 (xor_2_out, B2, Cin);
  Full_Adder full_adder_2 (.Cout(full_adder_2_cout), .B(xor_2_out), .A(A2), .S(S2), .Cin(full_adder_3_cout));
  xor xor_3 (xor_3_out, B1, Cin);
  Full_Adder full_adder_3 (.Cout(full_adder_3_cout), .B(xor_3_out), .A(A1), .S(S1), .Cin(full_adder_4_cout));
  xor xor_4 (xor_4_out, B0, Cin);
  Full_Adder full_adder_4 (.Cout(full_adder_4_cout), .B(xor_4_out), .A(A0), .S(S0), .Cin(Cin));
endmodule
