// Logisim project fulladder.circ as structural Verilog: 1 circuit, main circuit Full Adder
module Full_Adder (
  input  B,
  input  A,
  input  Cin,
  output Cout,
  output S
);

  wire and_1_out, and_2_out, xor_1_out;

  or or_1 (Cout, and_1_out, and_2_out);
  and and_1 (and_1_out, B, A);
  and and_2 (and_2_out, xor_1_out, Cin);
  xor xor_1 (xor_1_out, B, A);
  xor xor_2 (S, xor_1_out, Cin);
endmodule
